// Digital circuit 4bitprocessorPOST31.dig as structural Verilog
module _4bitprocessorPOST31 (
  input  clk,
  input  [1:0] IR,
  input  [1:0] MEM_ctrl,
  input  [3:0] MEM_input,
  input  [1:0] PC_ctrl,
  input  [15:0] temp,
  output [3:0] pc_output,
  output [15:0] instruct,
  output [3:0] ALU_output,
  output [3:0] read_2,
  output [3:0] read_1
);

  wire data_path_4bit_processorpost31alt_1_p9;
  wire [7:0] multiplexer_1_out, registerfile_write_ctrl_1_p2;

  // data_path_4bit_processorPOST31alt data_path_4bit_processorpost31alt_1: pin names not known; wires that end beside it: temp, clk, IR, PC_ctrl, MEM_ctrl, MEM_input, instruct, pc_output, data_path_4bit_processorpost31alt_1_p9
  // RegisterFile_Write_ctrl registerfile_write_ctrl_1: pin names not known; wires that end beside it: instruct[1:0], registerfile_write_ctrl_1_p2
  Multiplexer #(.Bits(8)) multiplexer_1 (
    .sel(data_path_4bit_processorpost31alt_1_p9), .in_0(registerfile_write_ctrl_1_p2), .in_1({8{1'b0}}),
    .out(multiplexer_1_out));
  Register_file register_file_1 (
    .Select_read1(instruct[5:4]), .Select_read2(instruct[3:2]), .clk(clk), .Write_Data(ALU_output),
    .Select_write(instruct[1:0]), .CTRL_registers(multiplexer_1_out), .Read_Data_1(read_1),
    .Read_Data_2(read_2));
  // ALU_R alu_r_1: pin names not known; wires that end beside it: instruct[8:6], read_2, read_1, ALU_output
endmodule

/* Test case testing:
clk IR MEM_ctrl MEM_input PC_ctrl pc_output instruct read_1 read_2 ALU_output
c 0 1 0x0 1 x x x x x
c 0 1 0x4 1 x x x x x
c 0 1 0x1 1 x x x x x
c 0 1 0x0 1 x x x x x

c 0 1 0x0 1 x x x x x
c 0 1 0x4 1 x x x x x
c 0 1 0x1 1 x x x x x
c 0 1 0x0 1 x x x x x

c 0 1 0x1 1 x x x x x
c 0 1 0x5 1 x x x x x
c 0 1 0x1 1 x x x x x
c 0 1 0x0 1 x x x x x

c 0 1 0x6 1 x x x x x
c 0 1 0x0 1 x x x x x
c 0 1 0x0 1 x x x x x
c 0 1 0x0 1 x x x x x


c 1 0 2 1 x x x x x
c 1 0 2 1 x x x x x
c 1 0 2 1 x x x x x
c 1 0 2 1 x x x x x
c 1 0 2 1 x x x x x
c 1 0 2 1 x x x x x
c 1 0 2 1 x x x x x
c 1 0 2 1 x x x x x
c 1 0 2 1 x x x x x
c 1 0 2 1 x x x x x
c 1 0 2 1 x x x x x
c 1 0 1 1 x x x x x
c 1 0 1 1 x x x x x
c 1 0 1 1 x x x x x
c 1 0 1 1 x x x x x
c 1 0 1 1 x x x x x
c 1 0 1 1 x x x x x
*/
