// Digital circuit data-path-4bit-processorPOST31alt.dig as structural Verilog
module data_path_4bit_processorPOST31alt (
  input  clk,
  input  [1:0] IR_ctrl,
  input  [1:0] pc_ctrl,
  input  [1:0] mem_ctrl,
  input  [3:0] Instr_mem_input,
  output [15:0] ir_out,
  output [3:0] pc_out
);

  wire and_1_out, not_1_out, not_2_out;
  wire [1:0] demultiplexer_1_out_0, demultiplexer_1_out_1, demultiplexer_1_out_2, demultiplexer_1_out_3;
  wire [3:0] demultiplexer_2_out_0, demultiplexer_2_out_1, demultiplexer_2_out_2, demultiplexer_2_out_3,
       gpr4_bit_1_p5, ir_1_p4, ir_2_p4, ir_3_p4, ir_4_p4;

  _4bitPC_final _4bitpc_final_1 (.Mux_controller(pc_ctrl), .clk(clk), .\output (pc_out));
  // GPR4_bit gpr4_bit_1: pin names not known; wires that end beside it: pc_out, clk, mem_ctrl, Instr_mem_input, gpr4_bit_1_p5
  Demultiplexer #(.Selector_Bits(2), .Bits(2)) demultiplexer_1 (
    .sel(pc_out[1:0]), .in(IR_ctrl), .out_0(demultiplexer_1_out_0), .out_1(demultiplexer_1_out_1),
    .out_2(demultiplexer_1_out_2), .out_3(demultiplexer_1_out_3));
  Demultiplexer #(.Selector_Bits(2), .Bits(4)) demultiplexer_2 (
    .sel(pc_out[1:0]), .in(gpr4_bit_1_p5), .out_0(demultiplexer_2_out_0), .out_1(demultiplexer_2_out_1),
    .out_2(demultiplexer_2_out_2), .out_3(demultiplexer_2_out_3));
  // IR ir_1: pin names not known; wires that end beside it: clk, demultiplexer_1_out_0, demultiplexer_2_out_0, ir_1_p4
  // IR ir_2: pin names not known; wires that end beside it: clk, demultiplexer_1_out_1, demultiplexer_2_out_1, ir_2_p4
  // IR ir_3: pin names not known; wires that end beside it: clk, demultiplexer_1_out_2, demultiplexer_2_out_2, ir_3_p4
  // IR ir_4: pin names not known; wires that end beside it: clk, demultiplexer_1_out_3, demultiplexer_2_out_3, ir_4_p4
  and and_1 (and_1_out, not_1_out, not_2_out);
  not not_1 (not_1_out, pc_out[0]);
  not not_2 (not_2_out, pc_out[1]);
  assign ir_out = and_1_out ? {ir_4_p4, ir_3_p4, ir_2_p4, ir_1_p4} : 16'bz;  // Driver driver_1
endmodule
